// Logisim project 4-Stage Pipeline Design.circ as structural Verilog: 1 circuit, main circuit main
module main (
  input  in_1,
  input  in_2,
  output out_3
);

  wire adder_1_cout, and_1_out, and_2_out, and_3_out, and_5_out, and_6_out, clock_1_out, comparator_1_eq,
       comparator_1_gt, comparator_1_lt, comparator_2_lt, demultiplexer_1_out0, demultiplexer_1_out1,
       demultiplexer_1_out2, demultiplexer_1_out3, demultiplexer_1_out4, demultiplexer_1_out5,
       demultiplexer_1_out6, demultiplexer_1_out7, demultiplexer_1_out8, demultiplexer_1_out9,
       demultiplexer_1_out10, demultiplexer_1_out11, demultiplexer_1_out12, demultiplexer_1_out13,
       demultiplexer_1_out14, demultiplexer_1_out15, demultiplexer_1_out16, demultiplexer_1_out17,
       demultiplexer_1_out18, demultiplexer_1_out19, demultiplexer_1_out20, demultiplexer_1_out21,
       demultiplexer_1_out22, demultiplexer_1_out23, demultiplexer_1_out24, demultiplexer_1_out25,
       demultiplexer_1_out26, demultiplexer_1_out27, demultiplexer_1_out28, demultiplexer_1_out29,
       demultiplexer_1_out30, demultiplexer_1_out31, not_1_out, not_2_out, not_3_out, not_4_out, not_5_out,
       not_6_out, not_7_out, not_8_out, or_1_out, shift_register_1_q0, shift_register_2_out,
       shift_register_2_q1, shift_register_2_q2, shift_register_2_q3, shift_register_2_q4, subtractor_1_bout;
  wire [1:0] shift_register_1_q2;
  wire [2:0] multiplexer_2_out, shift_register_1_q5;
  wire [4:0] multiplexer_3_out, shift_register_1_q10, shift_register_1_q15;
  wire [15:0] shift_register_1_q20;
  wire [31:0] adder_1_out, and_4_out, controlled_buffer_1_out, multiplexer_1_out, multiplexer_4_out,
       multiplexer_5_out, multiplexer_6_out, multiplexer_7_out, Offset_From_Register_Compatibility_q31,
       or_2_out, register_1_q, register_2_q, register_3_q, register_4_q, register_5_q, register_6_q,
       register_7_q, register_8_q, register_9_q, register_10_q, register_11_q, register_12_q, register_13_q,
       register_14_q, register_15_q, register_16_q, register_17_q, register_18_q, register_19_q,
       register_20_q, register_21_q, register_22_q, register_23_q, register_24_q, register_25_q,
       register_26_q, register_27_q, register_28_q, register_29_q, register_30_q, register_31_q,
       register_32_q, register_33_q, register_34_q, register_35_q, register_36_q, register_37_q,
       subtractor_1_out, xor_1_out;

  Clock clock_1 (.out(clock_1_out));
  not not_1 (not_1_out, shift_register_1_q0);
  not not_2 (not_2_out, shift_register_1_q5[0]);
  and and_1 (and_1_out, not_1_out, shift_register_2_q4);
  and and_2 (and_2_out, shift_register_1_q0, shift_register_2_q4, not_3_out, shift_register_1_q2[0], not_2_out);
  or or_1 (or_1_out, and_1_out, and_2_out);
  not not_3 (not_3_out, shift_register_1_q2[1]);
  Shift_Register #(.length(32)) shift_register_1 (
    .q0(shift_register_1_q0), .q1(shift_register_1_q2[1]), .q2(shift_register_1_q2[0]),
    .q3(shift_register_1_q5[2]), .q4(shift_register_1_q5[1]), .q5(shift_register_1_q5[0]),
    .q6(shift_register_1_q10[4]), .q7(shift_register_1_q10[3]), .q8(shift_register_1_q10[2]),
    .q9(shift_register_1_q10[1]), .q10(shift_register_1_q10[0]), .q11(shift_register_1_q15[4]),
    .q12(shift_register_1_q15[3]), .q13(shift_register_1_q15[2]), .q14(shift_register_1_q15[1]),
    .q15(shift_register_1_q15[0]), .q16(shift_register_1_q20[15]), .q17(shift_register_1_q20[14]),
    .q18(shift_register_1_q20[13]), .q19(shift_register_1_q20[12]), .q20(shift_register_1_q20[11]),
    .q21(shift_register_1_q20[10]), .q22(shift_register_1_q20[9]), .q23(shift_register_1_q20[8]),
    .q24(shift_register_1_q20[7]), .q25(shift_register_1_q20[6]), .q26(shift_register_1_q20[5]),
    .q27(shift_register_1_q20[4]), .q28(shift_register_1_q20[3]), .q29(shift_register_1_q20[2]),
    .q30(shift_register_1_q20[1]), .q31(shift_register_1_q20[0]));  // open: shift, in, clk, out, load, clr, d0, d1, d2, d3, d4, d5, d6, d7, d8, d9, d10, d11, d12, d13, d14, d15, d16, d17, d18, d19, d20, d21, d22, d23, d24, d25, d26, d27, d28, d29, d30, d31
  Shift_Register #(.length(5)) shift_register_2 (
    .in(shift_register_2_out), .clk(clock_1_out), .out(shift_register_2_out), .q1(shift_register_2_q1),
    .q2(shift_register_2_q2), .q3(shift_register_2_q3), .q4(shift_register_2_q4));  // open: shift, load, clr, d0, q0, d1, d2, d3, d4
  not not_4 (not_4_out, shift_register_1_q2[1]);
  not not_5 (not_5_out, shift_register_1_q5[2]);
  Demultiplexer #(.select(5)) demultiplexer_1 (
    .out0(demultiplexer_1_out0), .out1(demultiplexer_1_out1), .out2(demultiplexer_1_out2),
    .out3(demultiplexer_1_out3), .out4(demultiplexer_1_out4), .out5(demultiplexer_1_out5),
    .out6(demultiplexer_1_out6), .out7(demultiplexer_1_out7), .out8(demultiplexer_1_out8),
    .out9(demultiplexer_1_out9), .out10(demultiplexer_1_out10), .out11(demultiplexer_1_out11),
    .out12(demultiplexer_1_out12), .out13(demultiplexer_1_out13), .out14(demultiplexer_1_out14),
    .out15(demultiplexer_1_out15), .out16(demultiplexer_1_out16), .out17(demultiplexer_1_out17),
    .out18(demultiplexer_1_out18), .out19(demultiplexer_1_out19), .out20(demultiplexer_1_out20),
    .out21(demultiplexer_1_out21), .out22(demultiplexer_1_out22), .out23(demultiplexer_1_out23),
    .out24(demultiplexer_1_out24), .out25(demultiplexer_1_out25), .out26(demultiplexer_1_out26),
    .out27(demultiplexer_1_out27), .out28(demultiplexer_1_out28), .out29(demultiplexer_1_out29),
    .out30(demultiplexer_1_out30), .out31(demultiplexer_1_out31), .in(or_1_out), .sel(shift_register_1_q10));  // open: en
  not not_6 (not_6_out, shift_register_1_q5[1]);
  Multiplexer #(.select(5), .width(32)) multiplexer_1 (
    .in0(register_2_q), .in1(register_4_q), .in2(register_5_q), .in3(register_8_q), .in4(register_10_q),
    .in5(register_13_q), .in6(register_12_q), .in7(register_16_q), .in8(register_18_q), .in9(register_21_q),
    .in10(register_20_q), .in11(register_24_q), .in12(register_27_q), .in13(register_30_q),
    .in14(register_31_q), .in15(register_34_q), .in16(register_3_q), .in17(register_6_q),
    .in18(register_7_q), .in19(register_9_q), .in20(register_11_q), .in21(register_14_q),
    .in22(register_15_q), .in23(register_17_q), .in24(register_19_q), .in25(register_22_q),
    .in26(register_23_q), .in27(register_25_q), .in28(register_28_q), .in29(register_32_q),
    .in30(register_33_q), .in31(register_35_q), .out(multiplexer_1_out), .sel(shift_register_1_q15));  // open: en
  Register #(.width(32)) register_1 (
    .D(multiplexer_1_out), .Q(register_1_q), .clk(shift_register_2_q1));  // open: en, clr
  Multiplexer #(.width(3)) multiplexer_2 (
    .in0(shift_register_1_q5), .in1({3{in_2}}), .out(multiplexer_2_out), .sel(shift_register_1_q0));  // open: en
  Register #(.width(32)) register_2 (
    .D(register_29_q), .en(demultiplexer_1_out0), .Q(register_2_q), .clk(clock_1_out));  // open: clr
  Register #(.width(32)) register_3 (
    .D(register_29_q), .en(demultiplexer_1_out16), .Q(register_3_q), .clk(clock_1_out));  // open: clr
  and and_3 (and_3_out, shift_register_1_q5[0], not_6_out, not_5_out, shift_register_1_q2[0], not_4_out, shift_register_1_q0);
  Register #(.width(32)) register_4 (
    .D(register_29_q), .en(demultiplexer_1_out1), .Q(register_4_q), .clk(clock_1_out));  // open: clr
  Register #(.width(32)) register_5 (
    .D(register_29_q), .en(demultiplexer_1_out2), .Q(register_5_q), .clk(clock_1_out));  // open: clr
  Register #(.width(32)) register_6 (
    .D(register_29_q), .en(demultiplexer_1_out17), .Q(register_6_q), .clk(clock_1_out));  // open: clr
  Register #(.width(32)) register_7 (
    .D(register_29_q), .en(demultiplexer_1_out18), .Q(register_7_q), .clk(clock_1_out));  // open: clr
  Multiplexer #(.width(5)) multiplexer_3 (
    .in0(shift_register_1_q20[15:11]), .in1(shift_register_1_q10), .out(multiplexer_3_out), .sel(and_3_out));  // open: en
  Register #(.width(32)) register_8 (
    .D(register_29_q), .en(demultiplexer_1_out3), .Q(register_8_q), .clk(clock_1_out));  // open: clr
  Register #(.width(32)) register_9 (
    .D(register_29_q), .en(demultiplexer_1_out19), .Q(register_9_q), .clk(clock_1_out));  // open: clr
  Adder #(.width(32)) adder_1 (
    .a(register_1_q), .b(multiplexer_7_out), .out(adder_1_out), .cout(adder_1_cout));  // open: cin
  Subtractor #(.width(32)) subtractor_1 (
    .a(register_1_q), .b(multiplexer_7_out), .out(subtractor_1_out), .bout(subtractor_1_bout));  // open: bin
  assign and_4_out = register_1_q & multiplexer_7_out;  // AND_Gate and_4, 32 bits wide
  assign or_2_out = register_1_q | multiplexer_7_out;  // OR_Gate or_2, 32 bits wide
  assign xor_1_out = register_1_q ^ multiplexer_7_out;  // XOR_Gate xor_1, 32 bits wide
  Comparator #(.width(32)) comparator_1 (
    .a(register_1_q), .b(multiplexer_7_out), .gt(comparator_1_gt), .eq(comparator_1_eq), .lt(comparator_1_lt));
  Register #(.width(32)) register_10 (
    .D(register_29_q), .en(demultiplexer_1_out4), .Q(register_10_q), .clk(clock_1_out));  // open: clr
  Register #(.width(32)) register_11 (
    .D(register_29_q), .en(demultiplexer_1_out20), .Q(register_11_q), .clk(clock_1_out));  // open: clr
  Shift_Register #(.length(32)) shift_register_3 (
    .clk(shift_register_2_q2), .load(shift_register_2_q2), .d25(comparator_2_lt), .d26(out_3),
    .d27(subtractor_1_bout), .d28(adder_1_cout), .d29(comparator_1_lt), .d30(comparator_1_eq),
    .d31(comparator_1_gt));  // open: shift, in, out, clr, d0, q0, d1, q1, d2, q2, d3, q3, d4, q4, d5, q5, d6, q6, d7, q7, d8, q8, d9, q9, d10, q10, d11, q11, d12, q12, d13, q13, d14, q14, d15, q15, d16, q16, d17, q17, d18, q18, d19, q19, d20, q20, d21, q21, d22, q22, d23, q23, d24, q24, q25, q26, q27, q28, q29, q30, q31
  Register #(.width(32)) register_12 (
    .D(register_29_q), .en(demultiplexer_1_out6), .Q(register_12_q), .clk(clock_1_out));  // open: clr
  Register #(.width(32)) register_13 (
    .D(register_29_q), .en(demultiplexer_1_out5), .Q(register_13_q), .clk(clock_1_out));  // open: clr
  Register #(.width(32)) register_14 (
    .D(register_29_q), .en(demultiplexer_1_out21), .Q(register_14_q), .clk(clock_1_out));  // open: clr
  Register #(.width(32)) register_15 (
    .D(register_29_q), .en(demultiplexer_1_out22), .Q(register_15_q), .clk(clock_1_out));  // open: clr
  Multiplexer #(.select(3), .width(32)) multiplexer_4 (
    .in0(adder_1_out), .in2(subtractor_1_out), .in4(and_4_out), .in5(or_2_out), .in6(xor_1_out),
    .out(multiplexer_4_out), .sel(multiplexer_2_out));  // open: in1, in3, in7, en
  Register #(.width(32)) register_16 (
    .D(register_29_q), .en(demultiplexer_1_out7), .Q(register_16_q), .clk(clock_1_out));  // open: clr
  Register #(.width(32)) register_17 (
    .D(register_29_q), .en(demultiplexer_1_out23), .Q(register_17_q), .clk(clock_1_out));  // open: clr
  Register #(.width(32)) register_18 (
    .D(register_29_q), .en(demultiplexer_1_out8), .Q(register_18_q), .clk(clock_1_out));  // open: clr
  Register #(.width(32)) register_19 (
    .D(register_29_q), .en(demultiplexer_1_out24), .Q(register_19_q), .clk(clock_1_out));  // open: clr
  Comparator #(.width(32)) comparator_2 (
    .a(multiplexer_4_out), .b({32{in_2}}), .eq(out_3), .lt(comparator_2_lt));  // open: gt
  Register #(.width(32)) register_20 (
    .D(register_29_q), .en(demultiplexer_1_out10), .Q(register_20_q), .clk(clock_1_out));  // open: clr
  Register #(.width(32)) register_21 (
    .D(register_29_q), .en(demultiplexer_1_out9), .Q(register_21_q), .clk(clock_1_out));  // open: clr
  Register #(.width(32)) register_22 (
    .D(register_29_q), .en(demultiplexer_1_out25), .Q(register_22_q), .clk(clock_1_out));  // open: clr
  Register #(.width(32)) register_23 (
    .D(register_29_q), .en(demultiplexer_1_out26), .Q(register_23_q), .clk(clock_1_out));  // open: clr
  Register #(.width(32)) register_24 (
    .D(register_29_q), .en(demultiplexer_1_out11), .Q(register_24_q), .clk(clock_1_out));  // open: clr
  Register #(.width(32)) register_25 (
    .D(register_29_q), .en(demultiplexer_1_out27), .Q(register_25_q), .clk(clock_1_out));  // open: clr
  not not_7 (not_7_out, shift_register_2_q1);
  Register #(.width(32)) register_26 (
    .D(multiplexer_4_out), .Q(register_26_q), .clk(shift_register_2_q2));  // open: en, clr
  Register #(.width(32)) register_27 (
    .D(register_29_q), .en(demultiplexer_1_out12), .Q(register_27_q), .clk(clock_1_out));  // open: clr
  Register #(.width(32)) register_28 (
    .D(register_29_q), .en(demultiplexer_1_out28), .Q(register_28_q), .clk(clock_1_out));  // open: clr
  Multiplexer #(.width(32)) multiplexer_5 (
    .in0(register_26_q), .in1(controlled_buffer_1_out), .out(multiplexer_5_out), .sel(shift_register_1_q0));  // open: en
  Register #(.width(32), .trigger("falling")) register_29 (
    .D(multiplexer_5_out), .Q(register_29_q), .clk(shift_register_2_q3));  // open: en, clr
  Register #(.width(32)) register_30 (
    .D(register_29_q), .en(demultiplexer_1_out13), .Q(register_30_q), .clk(clock_1_out));  // open: clr
  Register #(.width(32)) register_31 (
    .D(register_29_q), .en(demultiplexer_1_out14), .Q(register_31_q), .clk(clock_1_out));  // open: clr
  Register #(.width(32)) register_32 (
    .D(register_29_q), .en(demultiplexer_1_out29), .Q(register_32_q), .clk(clock_1_out));  // open: clr
  Register #(.width(32)) register_33 (
    .D(register_29_q), .en(demultiplexer_1_out30), .Q(register_33_q), .clk(clock_1_out));  // open: clr
  Register #(.width(32)) register_34 (
    .D(register_29_q), .en(demultiplexer_1_out15), .Q(register_34_q), .clk(clock_1_out));  // open: clr
  Register #(.width(32)) register_35 (
    .D(register_29_q), .en(demultiplexer_1_out31), .Q(register_35_q), .clk(clock_1_out));  // open: clr
  Multiplexer #(.select(5), .width(32)) multiplexer_6 (
    .in0(register_2_q), .in1(register_4_q), .in2(register_5_q), .in3(register_8_q), .in4(register_10_q),
    .in5(register_13_q), .in6(register_12_q), .in7(register_16_q), .in8(register_18_q), .in9(register_21_q),
    .in10(register_20_q), .in11(register_24_q), .in12(register_27_q), .in13(register_30_q),
    .in14(register_31_q), .in15(register_34_q), .in16(register_3_q), .in17(register_6_q),
    .in18(register_7_q), .in19(register_9_q), .in20(register_11_q), .in21(register_14_q),
    .in22(register_15_q), .in23(register_17_q), .in24(register_19_q), .in25(register_22_q),
    .in26(register_23_q), .in27(register_25_q), .in28(register_28_q), .in29(register_32_q),
    .in30(register_33_q), .in31(register_35_q), .out(multiplexer_6_out), .sel(multiplexer_3_out));  // open: en
  and and_5 (and_5_out, shift_register_1_q2[0], not_7_out, shift_register_1_q0, shift_register_1_q5[0]);
  Register #(.width(32)) register_36 (
    .D(multiplexer_6_out), .Q(register_36_q), .clk(shift_register_2_q1));  // open: en, clr
  Multiplexer #(.select(2), .width(32)) multiplexer_7 (
    .in0({32{in_1}}), .in1({{16{in_1}}, shift_register_1_q20}), .in2(register_36_q),
    .in3(Offset_From_Register_Compatibility_q31), .out(multiplexer_7_out), .sel(shift_register_1_q2));  // open: en
  Shift_Register #(.length(32)) Offset_From_Register_Compatibility (
    .q0(Offset_From_Register_Compatibility_q31[31]), .q1(Offset_From_Register_Compatibility_q31[30]),
    .q2(Offset_From_Register_Compatibility_q31[29]), .q3(Offset_From_Register_Compatibility_q31[28]),
    .q4(Offset_From_Register_Compatibility_q31[27]), .q5(Offset_From_Register_Compatibility_q31[26]),
    .q6(Offset_From_Register_Compatibility_q31[25]), .q7(Offset_From_Register_Compatibility_q31[24]),
    .q8(Offset_From_Register_Compatibility_q31[23]), .q9(Offset_From_Register_Compatibility_q31[22]),
    .q10(Offset_From_Register_Compatibility_q31[21]), .q11(Offset_From_Register_Compatibility_q31[20]),
    .q12(Offset_From_Register_Compatibility_q31[19]), .q13(Offset_From_Register_Compatibility_q31[18]),
    .q14(Offset_From_Register_Compatibility_q31[17]), .q15(Offset_From_Register_Compatibility_q31[16]),
    .q16(Offset_From_Register_Compatibility_q31[15]), .q17(Offset_From_Register_Compatibility_q31[14]),
    .q18(Offset_From_Register_Compatibility_q31[13]), .q19(Offset_From_Register_Compatibility_q31[12]),
    .q20(Offset_From_Register_Compatibility_q31[11]), .q21(Offset_From_Register_Compatibility_q31[10]),
    .q22(Offset_From_Register_Compatibility_q31[9]), .q23(Offset_From_Register_Compatibility_q31[8]),
    .q24(Offset_From_Register_Compatibility_q31[7]), .q25(Offset_From_Register_Compatibility_q31[6]),
    .q26(Offset_From_Register_Compatibility_q31[5]), .q27(Offset_From_Register_Compatibility_q31[4]),
    .q28(Offset_From_Register_Compatibility_q31[3]), .q29(Offset_From_Register_Compatibility_q31[2]),
    .q30(Offset_From_Register_Compatibility_q31[1]), .q31(Offset_From_Register_Compatibility_q31[0]));  // open: shift, in, clk, out, load, clr, d0, d1, d2, d3, d4, d5, d6, d7, d8, d9, d10, d11, d12, d13, d14, d15, d16, d17, d18, d19, d20, d21, d22, d23, d24, d25, d26, d27, d28, d29, d30, d31
  and and_6 (and_6_out, shift_register_2_q2, clock_1_out);
  Register #(.width(32), .trigger("falling")) register_37 (
    .D(register_36_q), .Q(register_37_q), .clk(and_6_out));  // open: en, clr
  assign controlled_buffer_1_out = and_5_out ? register_37_q : 32'bz;  // Controlled_Buffer controlled_buffer_1
  not not_8 (not_8_out, and_5_out);
  RAM #(.addrWidth(16), .dataWidth(32)) ram_1 (
    .addr(register_26_q[15:0]), .data(controlled_buffer_1_out), .clk(shift_register_2_q3), .ld(not_8_out));  // open: sel, clr
endmodule
