// Logisim project ALU Design.circ as structural Verilog: 1 circuit, main circuit main
module main (
  input  [31:0] Pin_A,
  input  [31:0] Pin_B,
  input  [31:0] Immediate_Value,
  input  in_4,
  input  [2:0] in_5,
  output [31:0] out_6
);

  wire clock_1_out;
  wire [31:0] adder_1_out, AND_out, multiplexer_1_out, multiplexer_2_out, NAND_out, NOR_out, OR_out, Reg_A_q,
       Reg_B_q, subtractor_1_out;

  Clock clock_1 (.out(clock_1_out));
  Register #(.width(32)) Reg_A (.D(Pin_A), .Q(Reg_A_q), .clk(clock_1_out));  // open: en, clr
  Register #(.width(32)) Reg_B (.D(Pin_B), .Q(Reg_B_q), .clk(clock_1_out));  // open: en, clr
  Multiplexer #(.width(32)) multiplexer_1 (
    .in0(Reg_B_q), .in1(Immediate_Value), .out(multiplexer_1_out), .sel(in_4));  // open: en
  Adder #(.width(32)) adder_1 (.a(Reg_A_q), .b(multiplexer_1_out), .out(adder_1_out));  // open: cin, cout
  Subtractor #(.width(32)) subtractor_1 (
    .a(Reg_A_q), .b(multiplexer_1_out), .out(subtractor_1_out));  // open: bin, bout
  assign AND_out = Reg_A_q & multiplexer_1_out;  // AND_Gate AND, 32 bits wide
  assign OR_out = Reg_A_q | multiplexer_1_out;  // OR_Gate OR, 32 bits wide
  assign NAND_out = ~(Reg_A_q & multiplexer_1_out);  // NAND_Gate NAND, 32 bits wide
  assign NOR_out = ~(Reg_A_q | multiplexer_1_out);  // NOR_Gate NOR, 32 bits wide
  Multiplexer #(.select(3), .width(32)) multiplexer_2 (
    .in0(adder_1_out), .in1(subtractor_1_out), .in2(AND_out), .in3(OR_out), .in4(NAND_out), .in5(NOR_out),
    .out(multiplexer_2_out), .sel(in_5));  // open: in6, in7, en
  Register #(.width(32)) Reg_Result (.D(multiplexer_2_out), .Q(out_6), .clk(clock_1_out));  // open: en, clr
endmodule
