// Logisim project MOV operation.circ as structural Verilog: 1 circuit, main circuit main
module main (
  input  in_1,
  input  in_2,
  input  [2:0] TO,
  input  [2:0] FROM
);

  wire clock_1_out, decoder_1_out0, decoder_1_out1, decoder_1_out2, decoder_1_out3, decoder_1_out4,
       decoder_1_out5, decoder_1_out6, decoder_1_out7;
  wire [7:0] multiplexer_1_out, REG_000_q7, REG_001_q7, REG_002_q7, REG_003_q7, REG_004_q7, REG_005_q7,
       REG_006_q7, REG_007_q7;

  Decoder #(.select(3)) decoder_1 (
    .out0(decoder_1_out0), .out1(decoder_1_out1), .out2(decoder_1_out2), .out3(decoder_1_out3),
    .out4(decoder_1_out4), .out5(decoder_1_out5), .out6(decoder_1_out6), .out7(decoder_1_out7), .sel(TO),
    .en(in_2));
  Clock clock_1 (.out(clock_1_out));
  Shift_Register REG_000 (
    .shift(in_1), .clk(clock_1_out), .load(decoder_1_out0), .d0(multiplexer_1_out[7]), .q0(REG_000_q7[7]),
    .d1(multiplexer_1_out[6]), .q1(REG_000_q7[6]), .d2(multiplexer_1_out[5]), .q2(REG_000_q7[5]),
    .d3(multiplexer_1_out[4]), .q3(REG_000_q7[4]), .d4(multiplexer_1_out[3]), .q4(REG_000_q7[3]),
    .d5(multiplexer_1_out[2]), .q5(REG_000_q7[2]), .d6(multiplexer_1_out[1]), .q6(REG_000_q7[1]),
    .d7(multiplexer_1_out[0]), .q7(REG_000_q7[0]));  // open: in, out, clr
  Shift_Register REG_004 (
    .shift(in_1), .clk(clock_1_out), .load(decoder_1_out4), .d0(multiplexer_1_out[7]), .q0(REG_004_q7[7]),
    .d1(multiplexer_1_out[6]), .q1(REG_004_q7[6]), .d2(multiplexer_1_out[5]), .q2(REG_004_q7[5]),
    .d3(multiplexer_1_out[4]), .q3(REG_004_q7[4]), .d4(multiplexer_1_out[3]), .q4(REG_004_q7[3]),
    .d5(multiplexer_1_out[2]), .q5(REG_004_q7[2]), .d6(multiplexer_1_out[1]), .q6(REG_004_q7[1]),
    .d7(multiplexer_1_out[0]), .q7(REG_004_q7[0]));  // open: in, out, clr
  Shift_Register REG_001 (
    .shift(in_1), .clk(clock_1_out), .load(decoder_1_out1), .d0(multiplexer_1_out[7]), .q0(REG_001_q7[7]),
    .d1(multiplexer_1_out[6]), .q1(REG_001_q7[6]), .d2(multiplexer_1_out[5]), .q2(REG_001_q7[5]),
    .d3(multiplexer_1_out[4]), .q3(REG_001_q7[4]), .d4(multiplexer_1_out[3]), .q4(REG_001_q7[3]),
    .d5(multiplexer_1_out[2]), .q5(REG_001_q7[2]), .d6(multiplexer_1_out[1]), .q6(REG_001_q7[1]),
    .d7(multiplexer_1_out[0]), .q7(REG_001_q7[0]));  // open: in, out, clr
  Shift_Register REG_005 (
    .shift(in_1), .clk(clock_1_out), .load(decoder_1_out5), .d0(multiplexer_1_out[7]), .q0(REG_005_q7[7]),
    .d1(multiplexer_1_out[6]), .q1(REG_005_q7[6]), .d2(multiplexer_1_out[5]), .q2(REG_005_q7[5]),
    .d3(multiplexer_1_out[4]), .q3(REG_005_q7[4]), .d4(multiplexer_1_out[3]), .q4(REG_005_q7[3]),
    .d5(multiplexer_1_out[2]), .q5(REG_005_q7[2]), .d6(multiplexer_1_out[1]), .q6(REG_005_q7[1]),
    .d7(multiplexer_1_out[0]), .q7(REG_005_q7[0]));  // open: in, out, clr
  Shift_Register REG_002 (
    .shift(in_1), .clk(clock_1_out), .load(decoder_1_out2), .d0(multiplexer_1_out[7]), .q0(REG_002_q7[7]),
    .d1(multiplexer_1_out[6]), .q1(REG_002_q7[6]), .d2(multiplexer_1_out[5]), .q2(REG_002_q7[5]),
    .d3(multiplexer_1_out[4]), .q3(REG_002_q7[4]), .d4(multiplexer_1_out[3]), .q4(REG_002_q7[3]),
    .d5(multiplexer_1_out[2]), .q5(REG_002_q7[2]), .d6(multiplexer_1_out[1]), .q6(REG_002_q7[1]),
    .d7(multiplexer_1_out[0]), .q7(REG_002_q7[0]));  // open: in, out, clr
  Shift_Register REG_006 (
    .shift(in_1), .clk(clock_1_out), .load(decoder_1_out6), .d0(multiplexer_1_out[7]), .q0(REG_006_q7[7]),
    .d1(multiplexer_1_out[6]), .q1(REG_006_q7[6]), .d2(multiplexer_1_out[5]), .q2(REG_006_q7[5]),
    .d3(multiplexer_1_out[4]), .q3(REG_006_q7[4]), .d4(multiplexer_1_out[3]), .q4(REG_006_q7[3]),
    .d5(multiplexer_1_out[2]), .q5(REG_006_q7[2]), .d6(multiplexer_1_out[1]), .q6(REG_006_q7[1]),
    .d7(multiplexer_1_out[0]), .q7(REG_006_q7[0]));  // open: in, out, clr
  Shift_Register REG_003 (
    .shift(in_1), .clk(clock_1_out), .load(decoder_1_out3), .d0(multiplexer_1_out[7]), .q0(REG_003_q7[7]),
    .d1(multiplexer_1_out[6]), .q1(REG_003_q7[6]), .d2(multiplexer_1_out[5]), .q2(REG_003_q7[5]),
    .d3(multiplexer_1_out[4]), .q3(REG_003_q7[4]), .d4(multiplexer_1_out[3]), .q4(REG_003_q7[3]),
    .d5(multiplexer_1_out[2]), .q5(REG_003_q7[2]), .d6(multiplexer_1_out[1]), .q6(REG_003_q7[1]),
    .d7(multiplexer_1_out[0]), .q7(REG_003_q7[0]));  // open: in, out, clr
  Shift_Register REG_007 (
    .shift(in_1), .clk(clock_1_out), .load(decoder_1_out7), .d0(multiplexer_1_out[7]), .q0(REG_007_q7[7]),
    .d1(multiplexer_1_out[6]), .q1(REG_007_q7[6]), .d2(multiplexer_1_out[5]), .q2(REG_007_q7[5]),
    .d3(multiplexer_1_out[4]), .q3(REG_007_q7[4]), .d4(multiplexer_1_out[3]), .q4(REG_007_q7[3]),
    .d5(multiplexer_1_out[2]), .q5(REG_007_q7[2]), .d6(multiplexer_1_out[1]), .q6(REG_007_q7[1]),
    .d7(multiplexer_1_out[0]), .q7(REG_007_q7[0]));  // open: in, out, clr
  Multiplexer #(.select(3), .width(8)) multiplexer_1 (
    .in0(REG_000_q7), .in1(REG_001_q7), .in2(REG_002_q7), .in3(REG_003_q7), .in4(REG_004_q7),
    .in5(REG_005_q7), .in6(REG_006_q7), .in7(REG_007_q7), .out(multiplexer_1_out), .sel(FROM), .en(in_2));
endmodule
