// Logisim project Memory Read and Write Machine Cycle.circ as structural Verilog: 1 circuit, main circuit main
module main (
  input  in_1
);

  wire and_1_out, and_2_out, clock_1_out, Memory_Read_q0, Memory_Read_q1, Memory_Read_q2, Memory_Write_q0,
       Memory_Write_q1, not_1_out, not_2_out, or_1_out, shift_register_1_q0, shift_register_1_q1;
  wire [7:0] controlled_buffer_1_out, controlled_buffer_4_out, MDR_q;
  wire [15:0] MAR_q, register_1_q;

  Clock clock_1 (.out(clock_1_out));
  and and_1 (and_1_out, clock_1_out, or_1_out);
  not not_1 (not_1_out, in_1);
  Shift_Register #(.length(2)) shift_register_1 (
    .shift(in_1), .clk(clock_1_out), .load(not_1_out), .d0(in_1), .q0(shift_register_1_q0), .d1(in_1),
    .q1(shift_register_1_q1));  // open: in, out, clr
  Shift_Register #(.length(3)) Memory_Read (
    .in(shift_register_1_q1), .clk(clock_1_out), .q0(Memory_Read_q0), .q1(Memory_Read_q1), .q2(Memory_Read_q2));  // open: shift, out, load, clr, d0, d1, d2
  Shift_Register #(.length(3)) Memory_Write (
    .in(shift_register_1_q0), .clk(clock_1_out), .q0(Memory_Write_q0), .q1(Memory_Write_q1));  // open: shift, out, load, clr, d0, d1, d2, q2
  Register MDR (.D(controlled_buffer_1_out), .Q(MDR_q), .clk(Memory_Read_q2));  // open: en, clr
  Register #(.width(16)) MAR (.Q(MAR_q));  // open: D, en, clk, clr
  assign controlled_buffer_1_out = Memory_Write_q1 ? MDR_q : 8'bz;  // Controlled_Buffer controlled_buffer_1
  or or_1 (or_1_out, Memory_Write_q0, Memory_Read_q0);
  assign controlled_buffer_1_out = or_1_out ? MAR_q[7:0] : 8'bz;  // Controlled_Buffer controlled_buffer_2
  assign controlled_buffer_1_out = Memory_Read_q1 ? controlled_buffer_4_out : 8'bz;  // Controlled_Buffer controlled_buffer_3
  Register #(.width(16)) register_1 (
    .D({MAR_q[15:8], controlled_buffer_1_out}), .Q(register_1_q), .clk(and_1_out));  // open: en, clr
  assign controlled_buffer_4_out = Memory_Write_q1 ? controlled_buffer_1_out : 8'bz;  // Controlled_Buffer controlled_buffer_4
  and and_2 (and_2_out, Memory_Write_q1, not_2_out);
  RAM #(.addrWidth(16), .bus("separate")) ram_1 (
    .addr(register_1_q), .din(controlled_buffer_4_out), .data(controlled_buffer_4_out),
    .str(Memory_Write_q1), .clk(and_2_out), .ld(Memory_Read_q1));  // open: sel, clr
  not not_2 (not_2_out, clock_1_out);
endmodule
