// Logisim project Sequential multiplier.circ as structural Verilog: 1 circuit, main circuit main
module main (
  input  in_1
);

  wire adder_1_cout, clock_1_out, counter_1_q, MSB_of_Product_out, Multiplier_LSB_of_Product_q7,
       register_1_q, register_2_q;
  wire [7:0] adder_1_out, and_2_out, MSB_of_Product_q7, Multiplicand_q7;
  wire [7:7] and_1_out;

  Clock clock_1 (.out(clock_1_out));
  Counter #(.width(1), .max('h1)) counter_1 (.Q(counter_1_q), .clk(clock_1_out));  // open: load, D, count, carry, clr
  Register #(.width(1)) register_1 (.D(adder_1_cout), .Q(register_1_q), .clk(clock_1_out));  // open: en, clr
  Shift_Register MSB_of_Product (
    .in(register_1_q), .clk(clock_1_out), .out(MSB_of_Product_out), .load(counter_1_q), .d0(adder_1_out[7]),
    .q0(MSB_of_Product_q7[7]), .d1(adder_1_out[6]), .q1(MSB_of_Product_q7[6]), .d2(adder_1_out[5]),
    .q2(MSB_of_Product_q7[5]), .d3(adder_1_out[4]), .q3(MSB_of_Product_q7[4]), .d4(adder_1_out[3]),
    .q4(MSB_of_Product_q7[3]), .d5(adder_1_out[2]), .q5(MSB_of_Product_q7[2]), .d6(adder_1_out[1]),
    .q6(MSB_of_Product_q7[1]), .d7(adder_1_out[0]), .q7(MSB_of_Product_q7[0]));  // open: shift, clr
  Shift_Register Multiplier_LSB_of_Product (
    .in(register_2_q), .clk(counter_1_q), .q7(Multiplier_LSB_of_Product_q7));  // open: shift, out, load, clr, d0, q0, d1, q1, d2, q2, d3, q3, d4, q4, d5, q5, d6, q6, d7
  Register #(.width(1)) register_2 (.D(MSB_of_Product_out), .Q(register_2_q), .clk(clock_1_out));  // open: en, clr
  Shift_Register Multiplicand (
    .shift(in_1), .clk(clock_1_out), .q0(Multiplicand_q7[7]), .q1(Multiplicand_q7[6]),
    .q2(Multiplicand_q7[5]), .q3(Multiplicand_q7[4]), .q4(Multiplicand_q7[3]), .q5(Multiplicand_q7[2]),
    .q6(Multiplicand_q7[1]), .q7(Multiplicand_q7[0]));  // open: in, out, load, clr, d0, d1, d2, d3, d4, d5, d6, d7
  and and_1 (and_1_out[7], Multiplier_LSB_of_Product_q7, counter_1_q);
  assign and_2_out = Multiplicand_q7 & {8{and_1_out[7]}};  // AND_Gate and_2, 8 bits wide
  Adder adder_1 (.a(and_2_out), .b(MSB_of_Product_q7), .out(adder_1_out), .cout(adder_1_cout));  // open: cin
endmodule
